# Fritzing sketch schematic-stripboard (saved by Fritzing 0.9.0b)
stripboards: 1

parts:
  R1 = Resistor [tolerance=±5% resistance=470 package=THT]
  R2 = Resistor [tolerance=±5% resistance=470 package=THT]
  R3 = Resistor [tolerance=±5% resistance=470 package=THT]
  R4 = Resistor [tolerance=±5% resistance=470 package=THT]
  S1 = Pushbutton [package="[THT]"]
  R5 = Resistor [tolerance=±5% resistance=10k package=THT]
  LED1 = LED - 5mm [color="Red (633nm)" package="5 mm [THT]"]
  R6 = Resistor [tolerance=±5% resistance=470 package=THT]
  U1 = 7-SEGMENT-4DIGIT [part_number="Kyx 5461as" package=7-segment-4digit-youngsun]
  U2 = atmega328 [package=dip]

nets:
  N1: R1.Pin_1, U2.D7
  N2: R2.Pin_1, U2.A1
  N3: R3.Pin_1, U2.A2
  N4: R4.Pin_1, U2.A5
  N5: S1.Pin_1, S1.Pin_2, R5.Pin_1
  N6: S1.Pin_3, S1.Pin_4, U1.1, U1.2, U1.3, U1.4, U1.5, U1.6, U2.D2, U2.D3_(PWM), U2.D4, U2.GND#7, U2.AVCC
  N7: R5.Pin_0, R6.Pin_0, U2.D8, U2.GND#21
  N8: LED1.cathode, R6.Pin_1
  N9: LED1.anode, U2.D13
  N10: U1.7, U1.8, U1.9, U1.10, U1.11, U1.12, U2.D6_(PWM)
